# Fritzing sketch 회로구성 (saved by Fritzing 0.9.3b)
breadboards: 1

parts:
  아두이노 = Arduino Uno (Rev3)
  S1 = Pushbutton [package="[THT]"]  # not connected
  로드셀 = HX711 Weighing Sensor Module
  IC1 = DS1302 [package="SO8 [SMD]"]  # not connected

nets:
  GND: 아두이노.GND, 로드셀.GND
